// Logisim project 8-bit even parity generator _Logisim.circ as structural Verilog: 1 circuit, main circuit 8-bit Even Parity Generator
module _8_bit_Even_Parity_Generator (
  input  X7,
  input  X6,
  input  X5,
  input  X4,
  input  X3,
  input  X2,
  input  X1,
  input  X0,
  output C0,
  output C1,
  output C2,
  output C3,
  output C4,
  output C5,
  output C6,
  output C7,
  output C8,
  output C8_2,
  output C8_3,
  output C8_4,
  output C8_5,
  output C8_6,
  output C8_7,
  output C8_8
);

  wire xor_1_out, xor_2_out, xor_3_out, xor_4_out, xor_5_out, xor_6_out;

  xor xor_1 (xor_1_out, X0, X1);
  xor xor_2 (xor_2_out, xor_1_out, xor_3_out);
  xor xor_3 (xor_3_out, X2, X3);
  xor xor_4 (xor_4_out, X4, X5);
  xor xor_5 (xor_5_out, xor_4_out, xor_6_out);
  xor xor_6 (xor_6_out, X6, X7);
  xor xor_7 (C8_8, xor_2_out, xor_5_out);

  assign C0 = X0;
  assign C1 = X1;
  assign C2 = X2;
  assign C3 = X3;
  assign C4 = X4;
  assign C5 = X5;
  assign C6 = X6;
  assign C7 = X7;
  assign C8 = 1'b0;
  assign C8_2 = 1'b0;
  assign C8_3 = 1'b0;
  assign C8_4 = 1'b0;
  assign C8_5 = 1'b0;
  assign C8_6 = 1'b0;
  assign C8_7 = 1'b0;
endmodule
